# Fritzing sketch CameraShutter (saved by Fritzing 0.9.3b)
circuit board: 9.8465cm x 6.45344cm
breadboards: 1

parts:
  UNO = Arduino Uno (Rev3)
  LCD1 = LCD screen
  RTrimLCD = Trimmer Potentiometer [maximum_resistance=10kΩ package=THT]
  RLCD = Resistor [tolerance=±5% resistance=220 package=THT]
  SwitchMinus = Pushbutton [package="[THT]"]
  SwitchPlus = Pushbutton [package="[THT]"]
  RMenu = Resistor [tolerance=±5% resistance=10k package=THT]
  RMinus = Resistor [tolerance=±5% resistance=10k package=THT]
  RPlus = Resistor [tolerance=±5% resistance=10k package=THT]
  UShoot = Optocoupler [package=THT]
  UFocus = Optocoupler [package=THT]
  RFocusOcto = Resistor [tolerance=±5% resistance=220 package=THT]
  LEDShoot = LED - 3mm [color="Green (560nm)" package="3 mm [THT]"]
  RFocusLED = Resistor [tolerance=±5% resistance=220 package=THT]
  LEDFocus = LED - 3mm [color="Yellow (592nm)" package="3 mm [THT]"]
  SwitchMenu = Pushbutton [package="[THT]"]
  RShootLED = Resistor [tolerance=±5% resistance=220 package=THT]
  RShootOcto = Resistor [tolerance=±5% resistance=220 package=THT]
  JackConnector = longpad pin header, 3 pins [form="long pad"]
  CMenu = Electrolytic Capacitor [capacitance=100µF package="100 mil [THT, electrolytic]"]
  RCMenu = Resistor [tolerance=±5% resistance=1k package=THT]
  IC_TRG = Hex Inverter Schmitt Trigger SN74HC14 [package="DIP (Dual Inline)"]

nets:
  N1: UNO.A0, SwitchPlus.Pin_3, SwitchPlus.Pin_4, RPlus.Pin_0
  N2: UNO.A1, SwitchMinus.Pin_3, SwitchMinus.Pin_4, RMinus.Pin_0
  N3: UNO.D8, LCD1.DB7
  N4: UNO.D11_PWM/MOSI, LCD1.E
  N5: UNO.D12/MISO, LCD1.RS
  N6: UNO.D2, IC_TRG.1Y
  N7: UNO.D3_PWM, LCD1.DB6
  N8: UNO.D4, LCD1.DB5
  N9: UNO.D5_PWM, LCD1.DB4
  N10: UNO.D6_PWM, RShootOcto.Pin_0
  N11: UNO.D7, RFocusOcto.Pin_0
  5V: UNO.5V, LCD1.VDD, RTrimLCD.leg1, RLCD.Pin_1, SwitchMinus.Pin_1, SwitchMinus.Pin_2, SwitchPlus.Pin_1, SwitchPlus.Pin_2, RMenu.Pin_1, LEDShoot.anode, LEDFocus.anode, IC_TRG.VCC
  GND: UNO.GND, LCD1.VSS, LCD1.R/W, LCD1.LED-, RTrimLCD.leg2, RMinus.Pin_1, RPlus.Pin_1, UShoot.Pin_2, UShoot.Pin_4, UFocus.Pin_2, UFocus.Pin_4, SwitchMenu.Pin_1, SwitchMenu.Pin_2, JackConnector.pin3, CMenu.-, IC_TRG.GND
  N12: LCD1.V0, RTrimLCD.wiper
  N13: LCD1.LED+, RLCD.Pin_0
  N14: RMenu.Pin_0, CMenu.+, RCMenu.Pin_1
  N15: UShoot.Pin_1, RShootOcto.Pin_1
  N16: UShoot.Pin_5, RShootLED.Pin_1, JackConnector.pin2
  N17: UFocus.Pin_1, RFocusOcto.Pin_1
  N18: UFocus.Pin_5, RFocusLED.Pin_1, JackConnector.pin1
  N19: LEDShoot.cathode, RShootLED.Pin_0
  N20: RFocusLED.Pin_0, LEDFocus.cathode
  N21: SwitchMenu.Pin_3, SwitchMenu.Pin_4, RCMenu.Pin_0, IC_TRG.1A

notes:
  - Shutter (internal jack)
  - Focus (middle jack)
  - Common (external jack)
