# Fritzing sketch CameraShutterMicro (saved by Fritzing 0.9.3b)
circuit board: 8.30412cm x 5.00453cm
breadboards: 1

parts:
  LCD1 = LCD screen
  RTrimLCD = Trimmer Potentiometer [maximum_resistance=10kΩ package=THT]
  RLCD = Resistor [tolerance=±5% resistance=220 package=THT]
  SwitchMinus = Pushbutton [package="[THT]"]
  SwitchPlus = Pushbutton [package="[THT]"]
  RMenu = Resistor [tolerance=±5% resistance=10k package=THT]
  RMinus = Resistor [tolerance=±5% resistance=10k package=THT]
  RPlus = Resistor [tolerance=±5% resistance=10k package=THT]
  UShoot = Optocoupler [package=THT]
  UFocus = Optocoupler [package=THT]
  RFocusOcto = Resistor [tolerance=±5% resistance=220 package=THT]
  LEDShoot = LED - 3mm [color="Green (560nm)" package="3 mm [THT]"]
  RFocusLED = Resistor [tolerance=±5% resistance=220 package=THT]
  LEDFocus = LED - 3mm [color="Yellow (592nm)" package="3 mm [THT]"]
  SwitchMenu = Pushbutton [package="[THT]"]
  RShootLED = Resistor [tolerance=±5% resistance=220 package=THT]
  RShootOcto = Resistor [tolerance=±5% resistance=220 package=THT]
  Jack2_5 = longpad pin header, 3 pins [form="long pad"]
  CMenu = Electrolytic Capacitor [capacitance=100µF package="100 mil [THT, electrolytic]"]
  RCMenu = Resistor [tolerance=±5% resistance=1k package=THT]
  Arduino_Micro = Arduino Micro (Rev3)

nets:
  VSS: LCD1.VSS, LCD1.R/W, LCD1.LED-, RTrimLCD.leg2, RMinus.Pin_1, RPlus.Pin_1, UShoot.Pin_2, UShoot.Pin_4, UFocus.Pin_2, UFocus.Pin_4, SwitchMenu.Pin_1, SwitchMenu.Pin_2, Jack2_5.pin3, CMenu.-, Arduino_Micro.GND
  VDD: LCD1.VDD, RTrimLCD.leg1, RLCD.Pin_1, SwitchMinus.Pin_1, SwitchMinus.Pin_2, SwitchPlus.Pin_1, SwitchPlus.Pin_2, RMenu.Pin_1, LEDShoot.anode, LEDFocus.anode, Arduino_Micro.5V
  N1: LCD1.V0, RTrimLCD.wiper
  N2: LCD1.RS, Arduino_Micro.D12_PWM/A11
  N3: LCD1.E, Arduino_Micro.D11_PWM
  N4: LCD1.DB4, Arduino_Micro.D5_PWM
  N5: LCD1.DB5, Arduino_Micro.D4_PWM/A6
  N6: LCD1.DB6, Arduino_Micro.D3/SCL
  N7: LCD1.DB7, Arduino_Micro.D8_PWM/A8
  N8: LCD1.LED+, RLCD.Pin_0
  N9: SwitchMinus.Pin_3, SwitchMinus.Pin_4, RMinus.Pin_0, Arduino_Micro.A1
  N10: SwitchPlus.Pin_3, SwitchPlus.Pin_4, RPlus.Pin_0, Arduino_Micro.A0
  N11: RMenu.Pin_0, CMenu.+, RCMenu.Pin_1, Arduino_Micro.D2/SDA
  N12: UShoot.Pin_1, RShootOcto.Pin_1
  N13: UShoot.Pin_5, RShootLED.Pin_1, Jack2_5.pin2
  N14: UFocus.Pin_1, RFocusOcto.Pin_1
  N15: UFocus.Pin_5, RFocusLED.Pin_1, Jack2_5.pin1
  N16: RFocusOcto.Pin_0, Arduino_Micro.D7
  N17: LEDShoot.cathode, RShootLED.Pin_0
  N18: RFocusLED.Pin_0, LEDFocus.cathode
  N19: SwitchMenu.Pin_3, SwitchMenu.Pin_4, RCMenu.Pin_0
  N20: RShootOcto.Pin_0, Arduino_Micro.D6_PWM/A7

notes:
  - Shutter (internal jack)
  - Focus (middle jack)
  - Common (external jack)
